// Logisim project MIPS.circ as structural Verilog: 11 circuits, main circuit main
module main (
);

  wire ALU_zero, and_1_out, clock_1_out, Control_alusrc, Control_branch, Control_jump, Control_memread,
       Control_memtoreg, Control_memwrite, Control_regdst, Control_regwrite;
  wire [2:0] ALUControl_out_3;
  wire [4:0] adder_1_out, adder_2_out, multiplexer_1_out, multiplexer_2_out, multiplexer_4_out,
       reducirbits26_1_out_2, reducirbits_1_out_2, ReducirBits_2_out_2, register_1_q, Split__15_11,
       Split__20_16, Split__25_21;
  wire [5:0] Split__5_0, Split__31_26;
  wire [15:0] Split__15_0;
  wire [25:0] Split__25_0;
  wire [31:0] ALU_r, multiplexer_3_out, multiplexer_5_out, ram_1_data, Register_2_readdata1,
       Register_2_readdata2, rom_1_data, SignExtend_out_2;

  Register_part #(.width(5)) register_1 (.D(multiplexer_1_out), .Q(register_1_q), .clk(clock_1_out));  // open: en, clr
  Clock clock_1 (.out(clock_1_out));
  Adder #(.width(5)) adder_1 (.a(register_1_q), .b(5'b00001), .out(adder_1_out));  // open: cin, cout
  ROM #(.addrWidth(5), .dataWidth(32)) rom_1 (.addr(register_1_q), .data(rom_1_data));  // open: sel
  Dividir32 Split (
    .in_1(rom_1_data), ._31_26(Split__31_26), ._5_0(Split__5_0), ._25_21(Split__25_21),
    ._20_16(Split__20_16), ._15_11(Split__15_11), ._15_0(Split__15_0), ._25_0(Split__25_0));
  Multiplexer #(.width(5), .enable("false")) multiplexer_1 (
    .in0(multiplexer_4_out), .in1(reducirbits26_1_out_2), .out(multiplexer_1_out), .sel(Control_jump));
  Control Control (
    ._31_26(Split__31_26), ._5_0(Split__5_0), .RegDst(Control_regdst), .Branch(Control_branch),
    .MemRead(Control_memread), .MemtoReg(Control_memtoreg), .MemWrite(Control_memwrite),
    .ALUSrc(Control_alusrc), .RegWrite(Control_regwrite), .Jump(Control_jump));
  Multiplexer #(.width(5), .enable("false")) multiplexer_2 (
    .in0(Split__20_16), .in1(Split__15_11), .out(multiplexer_2_out), .sel(Control_regdst));
  SignExtend SignExtend (.in_1(Split__15_0), .out_2(SignExtend_out_2));
  ReducirBits26 reducirbits26_1 (.out_2(reducirbits26_1_out_2), .in_1(Split__25_0));
  Register Register_2 (
    .ReadRegister1(Split__25_21), .ReadRegister2(Split__20_16), .WriteRegister(multiplexer_2_out),
    .WriteData(multiplexer_5_out), .WriteEnable(Control_regwrite), .Clock(clock_1_out),
    .ReadData1(Register_2_readdata1), .ReadData2(Register_2_readdata2));
  ReducirBits reducirbits_1 (.in_1(SignExtend_out_2), .out_2(reducirbits_1_out_2));
  ALU ALU (.A(Register_2_readdata1), .B(multiplexer_3_out), .in_3(ALUControl_out_3), .Zero(ALU_zero), .R(ALU_r));
  Multiplexer #(.width(32), .enable("false")) multiplexer_3 (
    .in0(Register_2_readdata2), .in1(SignExtend_out_2), .out(multiplexer_3_out), .sel(Control_alusrc));
  ALUControl ALUControl (._31_26(Split__31_26), ._5_0(Split__5_0), .out_3(ALUControl_out_3));
  Adder #(.width(5)) adder_2 (.a(adder_1_out), .b(reducirbits_1_out_2), .out(adder_2_out));  // open: cin, cout
  and and_1 (and_1_out, Control_branch, ALU_zero);
  ReducirBits ReducirBits_2 (.in_1(ALU_r), .out_2(ReducirBits_2_out_2));
  Multiplexer #(.width(5), .enable("false")) multiplexer_4 (
    .in0(adder_1_out), .in1(adder_2_out), .out(multiplexer_4_out), .sel(and_1_out));
  RAM #(.addrWidth(5), .dataWidth(32), .bus("separate")) ram_1 (
    .addr(ReducirBits_2_out_2), .din(Register_2_readdata2), .data(ram_1_data), .str(Control_memwrite),
    .clk(clock_1_out), .ld(Control_memread));  // open: sel, clr
  Multiplexer #(.width(32), .enable("false")) multiplexer_5 (
    .in0(ALU_r), .in1(ram_1_data), .out(multiplexer_5_out), .sel(Control_memtoreg));

  // Notes on the sheet:
  //   contents of rom_1 (hex, n*v repeats v):
  //   820 24020009 8c230000 20210001 8c240000 83282a 10a00001 801820 10220001 8000003 ac230001 800000b
endmodule

module ALU (
  input  [31:0] A,
  input  [31:0] B,
  input  [2:0] in_3,
  output Zero,
  output [31:0] R
);

  wire comparator_1_lt;
  wire [31:0] adder_1_out, adder_2_out, and_1_out, multiplexer_1_out, not_1_out, or_1_out;

  Comparator #(.width(32)) comparator_1 (.a(A), .b(B), .lt(comparator_1_lt));  // open: gt, eq
  assign not_1_out = ~B;  // NOT_Gate not_1, 32 bits wide
  Adder #(.width(32)) adder_1 (.a(A), .b(B), .out(adder_1_out));  // open: cin, cout
  Adder #(.width(32)) adder_2 (.a(A), .b(not_1_out), .out(adder_2_out), .cin(1'b1));  // open: cout
  Multiplexer #(.width(32), .enable("false")) multiplexer_1 (
    .in0({32{1'b0}}), .in1(32'h1), .out(multiplexer_1_out), .sel(comparator_1_lt));
  assign and_1_out = A & B;  // AND_Gate and_1, 32 bits wide
  assign or_1_out = A | B;  // OR_Gate or_1, 32 bits wide
  Multiplexer #(.select(3), .width(32), .enable("false")) multiplexer_2 (
    .in0(and_1_out), .in1(or_1_out), .in2(adder_1_out), .in6(adder_2_out), .in7(multiplexer_1_out), .out(R),
    .sel(in_3));  // open: in3, in4, in5
  Comparator #(.width(32)) comparator_2 (.a({32{1'b0}}), .b(R), .eq(Zero));  // open: gt, lt
endmodule

module Control (
  input  [5:0] _31_26,
  input  [5:0] _5_0,
  output RegDst,
  output Branch,
  output MemRead,
  output MemtoReg,
  output MemWrite,
  output ALUSrc,
  output RegWrite,
  output Jump
);

  wire identifyop_1_add, identifyop_1_addi, identifyop_1_addiu, identifyop_1_and, identifyop_1_or,
       identifyop_1_slt, identifyop_1_sub;

  IdentifyOp identifyop_1 (
    ._31_26(_31_26), ._5_0(_5_0), .ADD(identifyop_1_add), .SLT(identifyop_1_slt), .ADDIU(identifyop_1_addiu),
    .LW(MemRead), .ADDI(identifyop_1_addi), .BEQ(Branch), .SW(MemWrite), .SUB(identifyop_1_sub),
    .AND(identifyop_1_and), .OR(identifyop_1_or), .J(Jump));
  or or_1 (RegDst, identifyop_1_add, identifyop_1_slt, identifyop_1_sub, identifyop_1_and, identifyop_1_or);
  or or_2 (ALUSrc, identifyop_1_addiu, MemRead, identifyop_1_addi, MemWrite);
  or or_3 (RegWrite, identifyop_1_add, identifyop_1_slt, identifyop_1_addiu, MemRead, identifyop_1_addi, identifyop_1_sub, identifyop_1_and, identifyop_1_or);

  assign MemtoReg = MemRead;
endmodule

module IdentifyOp (
  input  [5:0] _31_26,
  input  [5:0] _5_0,
  output ADD,
  output SLT,
  output ADDIU,
  output LW,
  output ADDI,
  output BEQ,
  output SW,
  output SUB,
  output AND,
  output OR,
  output J
);

  wire _000000_out, and_1_out, and_2_out, and_3_out, and_4_out, and_5_out, not_1_out, not_2_out, not_3_out,
       not_4_out, not_5_out, not_6_out, not_7_out, not_8_out, not_9_out, not_10_out, not_11_out, not_12_out,
       not_13_out, not_14_out, not_15_out, not_16_out, not_17_out, not_18_out, not_19_out, not_20_out,
       not_21_out, not_22_out, not_23_out, not_24_out, not_25_out, not_26_out, not_27_out, not_28_out,
       not_29_out, not_30_out, not_31_out, not_32_out, not_33_out, not_34_out, not_35_out, not_36_out,
       not_37_out, not_38_out, not_39_out, not_40_out, not_41_out, not_42_out, not_43_out, not_44_out,
       not_45_out, not_46_out, not_47_out, not_48_out, not_49_out;

  not not_1 (not_1_out, _31_26[5]);
  not not_2 (not_2_out, _31_26[4]);
  not not_3 (not_3_out, _31_26[3]);
  not not_4 (not_4_out, _31_26[2]);
  not not_5 (not_5_out, _31_26[1]);
  not not_6 (not_6_out, _31_26[0]);
  and _000000 (_000000_out, not_1_out, not_2_out, not_3_out, not_4_out, not_5_out, not_6_out);
  not not_7 (not_7_out, _5_0[4]);
  not not_8 (not_8_out, _5_0[3]);
  not not_9 (not_9_out, _5_0[2]);
  not not_10 (not_10_out, _5_0[1]);
  not not_11 (not_11_out, _5_0[0]);
  not not_12 (not_12_out, _5_0[4]);
  not not_13 (not_13_out, _5_0[2]);
  not not_14 (not_14_out, _5_0[0]);
  not not_15 (not_15_out, _31_26[5]);
  not not_16 (not_16_out, _31_26[4]);
  not not_17 (not_17_out, _31_26[2]);
  not not_18 (not_18_out, _31_26[1]);
  not not_19 (not_19_out, _31_26[4]);
  not not_20 (not_20_out, _31_26[3]);
  not not_21 (not_21_out, _31_26[2]);
  not not_22 (not_22_out, _31_26[5]);
  not not_23 (not_23_out, _31_26[4]);
  not not_24 (not_24_out, _31_26[2]);
  not not_25 (not_25_out, _31_26[1]);
  not not_26 (not_26_out, _31_26[0]);
  not not_27 (not_27_out, _31_26[5]);
  not not_28 (not_28_out, _31_26[4]);
  not not_29 (not_29_out, _31_26[3]);
  not not_30 (not_30_out, _31_26[1]);
  not not_31 (not_31_out, _31_26[0]);
  not not_32 (not_32_out, _31_26[4]);
  not not_33 (not_33_out, _31_26[2]);
  not not_34 (not_34_out, _31_26[5]);
  not not_35 (not_35_out, _31_26[4]);
  not not_36 (not_36_out, _31_26[3]);
  not not_37 (not_37_out, _31_26[2]);
  not not_38 (not_38_out, _31_26[0]);
  and and_1 (and_1_out, _5_0[5], not_7_out, not_8_out, not_9_out, not_10_out, not_11_out);
  and and_2 (and_2_out, _5_0[5], not_12_out, _5_0[3], not_13_out, _5_0[1], not_14_out);
  and u_ADDIU (ADDIU, not_15_out, not_16_out, _31_26[3], not_17_out, not_18_out, _31_26[0]);
  and u_LW (LW, _31_26[5], not_19_out, not_20_out, not_21_out, _31_26[1], _31_26[0]);
  and u_ADDI (ADDI, not_22_out, not_23_out, _31_26[3], not_24_out, not_25_out, not_26_out);
  and u_BEQ (BEQ, not_27_out, not_28_out, not_29_out, _31_26[2], not_30_out, not_31_out);
  and u_SW (SW, _31_26[5], not_32_out, _31_26[3], not_33_out, _31_26[1], _31_26[0]);
  and u_J (J, not_34_out, not_35_out, not_36_out, not_37_out, _31_26[1], not_38_out);
  not not_39 (not_39_out, _5_0[4]);
  not not_40 (not_40_out, _5_0[3]);
  not not_41 (not_41_out, _5_0[2]);
  not not_42 (not_42_out, _5_0[0]);
  not not_43 (not_43_out, _5_0[4]);
  not not_44 (not_44_out, _5_0[3]);
  not not_45 (not_45_out, _5_0[1]);
  not not_46 (not_46_out, _5_0[0]);
  not not_47 (not_47_out, _5_0[4]);
  not not_48 (not_48_out, _5_0[3]);
  not not_49 (not_49_out, _5_0[1]);
  and u_ADD (ADD, _000000_out, and_1_out);
  and u_SLT (SLT, _000000_out, and_2_out);
  and and_3 (and_3_out, _5_0[5], not_39_out, not_40_out, not_41_out, _5_0[1], not_42_out);
  and and_4 (and_4_out, _5_0[5], not_43_out, not_44_out, _5_0[2], not_45_out, not_46_out);
  and and_5 (and_5_out, _5_0[5], not_47_out, not_48_out, _5_0[2], not_49_out, _5_0[0]);
  and u_SUB (SUB, _000000_out, and_3_out);
  and AND_6 (AND, _000000_out, and_4_out);
  and u_OR (OR, _000000_out, and_5_out);
endmodule

module Dividir32 (
  input  [31:0] in_1,
  output [5:0] _31_26,
  output [5:0] _5_0,
  output [4:0] _25_21,
  output [4:0] _20_16,
  output [4:0] _15_11,
  output [15:0] _15_0,
  output [25:0] _25_0
);


  assign _5_0 = in_1[5:0];
  assign _15_0 = in_1[15:0];
  assign _15_11 = in_1[15:11];
  assign _20_16 = in_1[20:16];
  assign _25_0 = in_1[25:0];
  assign _25_21 = in_1[25:21];
  assign _31_26 = in_1[31:26];
endmodule

module DataMemory (
  input  MemWrite,
  input  [4:0] Address,
  input  MemRead,
  input  [31:0] WriteData,
  input  Clock,
  output [31:0] ReadData
);

  wire decoder_1_out0, decoder_1_out1, decoder_1_out2, decoder_1_out3, decoder_1_out4, decoder_1_out5,
       decoder_1_out6, decoder_1_out7, decoder_1_out8, decoder_1_out9, decoder_1_out10, decoder_1_out11,
       decoder_1_out12, decoder_1_out13, decoder_1_out14, decoder_1_out15, decoder_1_out16, decoder_1_out17,
       decoder_1_out18, decoder_1_out19, decoder_1_out20, decoder_1_out21, decoder_1_out22, decoder_1_out23,
       decoder_1_out24, decoder_1_out25, decoder_1_out26, decoder_1_out27, decoder_1_out28, decoder_1_out29,
       decoder_1_out30, decoder_1_out31;
  wire [31:0] register_1_q, register_2_q, register_3_q, register_4_q, register_5_q, register_6_q,
       register_7_q, register_8_q, register_9_q, register_10_q, register_11_q, register_12_q, register_13_q,
       register_14_q, register_15_q, register_16_q, register_17_q, register_18_q, register_19_q,
       register_20_q, register_21_q, register_22_q, register_23_q, register_24_q, register_25_q,
       register_26_q, register_27_q, register_28_q, register_29_q, register_30_q, register_31_q,
       register_32_q;

  Decoder #(.select(5), .disabled(0)) decoder_1 (
    .out0(decoder_1_out0), .out1(decoder_1_out1), .out2(decoder_1_out2), .out3(decoder_1_out3),
    .out4(decoder_1_out4), .out5(decoder_1_out5), .out6(decoder_1_out6), .out7(decoder_1_out7),
    .out8(decoder_1_out8), .out9(decoder_1_out9), .out10(decoder_1_out10), .out11(decoder_1_out11),
    .out12(decoder_1_out12), .out13(decoder_1_out13), .out14(decoder_1_out14), .out15(decoder_1_out15),
    .out16(decoder_1_out16), .out17(decoder_1_out17), .out18(decoder_1_out18), .out19(decoder_1_out19),
    .out20(decoder_1_out20), .out21(decoder_1_out21), .out22(decoder_1_out22), .out23(decoder_1_out23),
    .out24(decoder_1_out24), .out25(decoder_1_out25), .out26(decoder_1_out26), .out27(decoder_1_out27),
    .out28(decoder_1_out28), .out29(decoder_1_out29), .out30(decoder_1_out30), .out31(decoder_1_out31),
    .sel(Address), .en(MemWrite));
  Register_part #(.width(32)) register_1 (
    .D(WriteData), .en(decoder_1_out0), .Q(register_1_q), .clk(Clock));  // open: clr
  Register_part #(.width(32)) register_2 (
    .D(WriteData), .en(decoder_1_out1), .Q(register_2_q), .clk(Clock));  // open: clr
  Register_part #(.width(32)) register_3 (
    .D(WriteData), .en(decoder_1_out2), .Q(register_3_q), .clk(Clock));  // open: clr
  Register_part #(.width(32)) register_4 (
    .D(WriteData), .en(decoder_1_out3), .Q(register_4_q), .clk(Clock));  // open: clr
  Register_part #(.width(32)) register_5 (
    .D(WriteData), .en(decoder_1_out4), .Q(register_5_q), .clk(Clock));  // open: clr
  Register_part #(.width(32)) register_6 (
    .D(WriteData), .en(decoder_1_out5), .Q(register_6_q), .clk(Clock));  // open: clr
  Register_part #(.width(32)) register_7 (
    .D(WriteData), .en(decoder_1_out6), .Q(register_7_q), .clk(Clock));  // open: clr
  Register_part #(.width(32)) register_8 (
    .D(WriteData), .en(decoder_1_out7), .Q(register_8_q), .clk(Clock));  // open: clr
  Register_part #(.width(32)) register_9 (
    .D(WriteData), .en(decoder_1_out8), .Q(register_9_q), .clk(Clock));  // open: clr
  Register_part #(.width(32)) register_10 (
    .D(WriteData), .en(decoder_1_out9), .Q(register_10_q), .clk(Clock));  // open: clr
  Register_part #(.width(32)) register_11 (
    .D(WriteData), .en(decoder_1_out10), .Q(register_11_q), .clk(Clock));  // open: clr
  Register_part #(.width(32)) register_12 (
    .D(WriteData), .en(decoder_1_out11), .Q(register_12_q), .clk(Clock));  // open: clr
  Register_part #(.width(32)) register_13 (
    .D(WriteData), .en(decoder_1_out12), .Q(register_13_q), .clk(Clock));  // open: clr
  Register_part #(.width(32)) register_14 (
    .D(WriteData), .en(decoder_1_out13), .Q(register_14_q), .clk(Clock));  // open: clr
  Register_part #(.width(32)) register_15 (
    .D(WriteData), .en(decoder_1_out14), .Q(register_15_q), .clk(Clock));  // open: clr
  Register_part #(.width(32)) register_16 (
    .D(WriteData), .en(decoder_1_out15), .Q(register_16_q), .clk(Clock));  // open: clr
  Register_part #(.width(32)) register_17 (
    .D(WriteData), .en(decoder_1_out16), .Q(register_17_q), .clk(Clock));  // open: clr
  Register_part #(.width(32)) register_18 (
    .D(WriteData), .en(decoder_1_out17), .Q(register_18_q), .clk(Clock));  // open: clr
  Register_part #(.width(32)) register_19 (
    .D(WriteData), .en(decoder_1_out18), .Q(register_19_q), .clk(Clock));  // open: clr
  Register_part #(.width(32)) register_20 (
    .D(WriteData), .en(decoder_1_out19), .Q(register_20_q), .clk(Clock));  // open: clr
  Register_part #(.width(32)) register_21 (
    .D(WriteData), .en(decoder_1_out20), .Q(register_21_q), .clk(Clock));  // open: clr
  Register_part #(.width(32)) register_22 (
    .D(WriteData), .en(decoder_1_out21), .Q(register_22_q), .clk(Clock));  // open: clr
  Register_part #(.width(32)) register_23 (
    .D(WriteData), .en(decoder_1_out22), .Q(register_23_q), .clk(Clock));  // open: clr
  Register_part #(.width(32)) register_24 (
    .D(WriteData), .en(decoder_1_out23), .Q(register_24_q), .clk(Clock));  // open: clr
  Register_part #(.width(32)) register_25 (
    .D(WriteData), .en(decoder_1_out24), .Q(register_25_q), .clk(Clock));  // open: clr
  Register_part #(.width(32)) register_26 (
    .D(WriteData), .en(decoder_1_out25), .Q(register_26_q), .clk(Clock));  // open: clr
  Register_part #(.width(32)) register_27 (
    .D(WriteData), .en(decoder_1_out26), .Q(register_27_q), .clk(Clock));  // open: clr
  Register_part #(.width(32)) register_28 (
    .D(WriteData), .en(decoder_1_out27), .Q(register_28_q), .clk(Clock));  // open: clr
  Register_part #(.width(32)) register_29 (
    .D(WriteData), .en(decoder_1_out28), .Q(register_29_q), .clk(Clock));  // open: clr
  Register_part #(.width(32)) register_30 (
    .D(WriteData), .en(decoder_1_out29), .Q(register_30_q), .clk(Clock));  // open: clr
  Register_part #(.width(32)) register_31 (
    .D(WriteData), .en(decoder_1_out30), .Q(register_31_q), .clk(Clock));  // open: clr
  Register_part #(.width(32)) register_32 (
    .D(WriteData), .en(decoder_1_out31), .Q(register_32_q), .clk(Clock));  // open: clr
  Multiplexer #(.select(5), .width(32), .disabled(0)) multiplexer_1 (
    .in0(register_1_q), .in1(register_2_q), .in2(register_3_q), .in3(register_4_q), .in4(register_5_q),
    .in5(register_6_q), .in6(register_7_q), .in7(register_8_q), .in8(register_9_q), .in9(register_10_q),
    .in10(register_11_q), .in11(register_12_q), .in12(register_13_q), .in13(register_14_q),
    .in14(register_15_q), .in15(register_16_q), .in16(register_17_q), .in17(register_18_q),
    .in18(register_19_q), .in19(register_20_q), .in20(register_21_q), .in21(register_22_q),
    .in22(register_23_q), .in23(register_24_q), .in24(register_25_q), .in25(register_26_q),
    .in26(register_27_q), .in27(register_28_q), .in28(register_29_q), .in29(register_30_q),
    .in30(register_31_q), .in31(register_32_q), .out(ReadData), .sel(Address), .en(MemRead));
endmodule

module Register (
  input  WriteEnable,
  input  [4:0] ReadRegister1,
  input  [4:0] ReadRegister2,
  input  [4:0] WriteRegister,
  input  [31:0] WriteData,
  input  Clock,
  output [31:0] ReadData1,
  output [31:0] ReadData2
);

  wire decoder_1_out0, decoder_1_out1, decoder_1_out2, decoder_1_out3, decoder_1_out4, decoder_1_out5,
       decoder_1_out6, decoder_1_out7, decoder_1_out8, decoder_1_out9, decoder_1_out10, decoder_1_out11,
       decoder_1_out12, decoder_1_out13, decoder_1_out14, decoder_1_out15, decoder_1_out16, decoder_1_out17,
       decoder_1_out18, decoder_1_out19, decoder_1_out20, decoder_1_out21, decoder_1_out22, decoder_1_out23,
       decoder_1_out24, decoder_1_out25, decoder_1_out26, decoder_1_out27, decoder_1_out28, decoder_1_out29,
       decoder_1_out30, decoder_1_out31;
  wire [31:0] register_1_q, register_2_q, register_3_q, register_4_q, register_5_q, register_6_q,
       register_7_q, register_8_q, register_9_q, register_10_q, register_11_q, register_12_q, register_13_q,
       register_14_q, register_15_q, register_16_q, register_17_q, register_18_q, register_19_q,
       register_20_q, register_21_q, register_22_q, register_23_q, register_24_q, register_25_q,
       register_26_q, register_27_q, register_28_q, register_29_q, register_30_q, register_31_q,
       register_32_q;

  Decoder #(.select(5), .disabled(0)) decoder_1 (
    .out0(decoder_1_out0), .out1(decoder_1_out1), .out2(decoder_1_out2), .out3(decoder_1_out3),
    .out4(decoder_1_out4), .out5(decoder_1_out5), .out6(decoder_1_out6), .out7(decoder_1_out7),
    .out8(decoder_1_out8), .out9(decoder_1_out9), .out10(decoder_1_out10), .out11(decoder_1_out11),
    .out12(decoder_1_out12), .out13(decoder_1_out13), .out14(decoder_1_out14), .out15(decoder_1_out15),
    .out16(decoder_1_out16), .out17(decoder_1_out17), .out18(decoder_1_out18), .out19(decoder_1_out19),
    .out20(decoder_1_out20), .out21(decoder_1_out21), .out22(decoder_1_out22), .out23(decoder_1_out23),
    .out24(decoder_1_out24), .out25(decoder_1_out25), .out26(decoder_1_out26), .out27(decoder_1_out27),
    .out28(decoder_1_out28), .out29(decoder_1_out29), .out30(decoder_1_out30), .out31(decoder_1_out31),
    .sel(WriteRegister), .en(WriteEnable));
  Register_part #(.width(32)) register_1 (
    .D(WriteData), .en(decoder_1_out0), .Q(register_1_q), .clk(Clock));  // open: clr
  Register_part #(.width(32)) register_2 (
    .D(WriteData), .en(decoder_1_out1), .Q(register_2_q), .clk(Clock));  // open: clr
  Register_part #(.width(32)) register_3 (
    .D(WriteData), .en(decoder_1_out2), .Q(register_3_q), .clk(Clock));  // open: clr
  Register_part #(.width(32)) register_4 (
    .D(WriteData), .en(decoder_1_out3), .Q(register_4_q), .clk(Clock));  // open: clr
  Register_part #(.width(32)) register_5 (
    .D(WriteData), .en(decoder_1_out4), .Q(register_5_q), .clk(Clock));  // open: clr
  Register_part #(.width(32)) register_6 (
    .D(WriteData), .en(decoder_1_out5), .Q(register_6_q), .clk(Clock));  // open: clr
  Register_part #(.width(32)) register_7 (
    .D(WriteData), .en(decoder_1_out6), .Q(register_7_q), .clk(Clock));  // open: clr
  Register_part #(.width(32)) register_8 (
    .D(WriteData), .en(decoder_1_out7), .Q(register_8_q), .clk(Clock));  // open: clr
  Register_part #(.width(32)) register_9 (
    .D(WriteData), .en(decoder_1_out8), .Q(register_9_q), .clk(Clock));  // open: clr
  Register_part #(.width(32)) register_10 (
    .D(WriteData), .en(decoder_1_out9), .Q(register_10_q), .clk(Clock));  // open: clr
  Register_part #(.width(32)) register_11 (
    .D(WriteData), .en(decoder_1_out10), .Q(register_11_q), .clk(Clock));  // open: clr
  Register_part #(.width(32)) register_12 (
    .D(WriteData), .en(decoder_1_out11), .Q(register_12_q), .clk(Clock));  // open: clr
  Register_part #(.width(32)) register_13 (
    .D(WriteData), .en(decoder_1_out12), .Q(register_13_q), .clk(Clock));  // open: clr
  Register_part #(.width(32)) register_14 (
    .D(WriteData), .en(decoder_1_out13), .Q(register_14_q), .clk(Clock));  // open: clr
  Register_part #(.width(32)) register_15 (
    .D(WriteData), .en(decoder_1_out14), .Q(register_15_q), .clk(Clock));  // open: clr
  Register_part #(.width(32)) register_16 (
    .D(WriteData), .en(decoder_1_out15), .Q(register_16_q), .clk(Clock));  // open: clr
  Register_part #(.width(32)) register_17 (
    .D(WriteData), .en(decoder_1_out16), .Q(register_17_q), .clk(Clock));  // open: clr
  Register_part #(.width(32)) register_18 (
    .D(WriteData), .en(decoder_1_out17), .Q(register_18_q), .clk(Clock));  // open: clr
  Register_part #(.width(32)) register_19 (
    .D(WriteData), .en(decoder_1_out18), .Q(register_19_q), .clk(Clock));  // open: clr
  Register_part #(.width(32)) register_20 (
    .D(WriteData), .en(decoder_1_out19), .Q(register_20_q), .clk(Clock));  // open: clr
  Register_part #(.width(32)) register_21 (
    .D(WriteData), .en(decoder_1_out20), .Q(register_21_q), .clk(Clock));  // open: clr
  Register_part #(.width(32)) register_22 (
    .D(WriteData), .en(decoder_1_out21), .Q(register_22_q), .clk(Clock));  // open: clr
  Register_part #(.width(32)) register_23 (
    .D(WriteData), .en(decoder_1_out22), .Q(register_23_q), .clk(Clock));  // open: clr
  Register_part #(.width(32)) register_24 (
    .D(WriteData), .en(decoder_1_out23), .Q(register_24_q), .clk(Clock));  // open: clr
  Register_part #(.width(32)) register_25 (
    .D(WriteData), .en(decoder_1_out24), .Q(register_25_q), .clk(Clock));  // open: clr
  Register_part #(.width(32)) register_26 (
    .D(WriteData), .en(decoder_1_out25), .Q(register_26_q), .clk(Clock));  // open: clr
  Register_part #(.width(32)) register_27 (
    .D(WriteData), .en(decoder_1_out26), .Q(register_27_q), .clk(Clock));  // open: clr
  Register_part #(.width(32)) register_28 (
    .D(WriteData), .en(decoder_1_out27), .Q(register_28_q), .clk(Clock));  // open: clr
  Register_part #(.width(32)) register_29 (
    .D(WriteData), .en(decoder_1_out28), .Q(register_29_q), .clk(Clock));  // open: clr
  Register_part #(.width(32)) register_30 (
    .D(WriteData), .en(decoder_1_out29), .Q(register_30_q), .clk(Clock));  // open: clr
  Register_part #(.width(32)) register_31 (
    .D(WriteData), .en(decoder_1_out30), .Q(register_31_q), .clk(Clock));  // open: clr
  Register_part #(.width(32)) register_32 (
    .D(WriteData), .en(decoder_1_out31), .Q(register_32_q), .clk(Clock));  // open: clr
  Multiplexer #(.select(5), .width(32), .disabled(0), .enable("false")) multiplexer_1 (
    .in0(register_1_q), .in1(register_2_q), .in2(register_3_q), .in3(register_4_q), .in4(register_5_q),
    .in5(register_6_q), .in6(register_7_q), .in7(register_8_q), .in8(register_9_q), .in9(register_10_q),
    .in10(register_11_q), .in11(register_12_q), .in12(register_13_q), .in13(register_14_q),
    .in14(register_15_q), .in15(register_16_q), .in16(register_17_q), .in17(register_18_q),
    .in18(register_19_q), .in19(register_20_q), .in20(register_21_q), .in21(register_22_q),
    .in22(register_23_q), .in23(register_24_q), .in24(register_25_q), .in25(register_26_q),
    .in26(register_27_q), .in27(register_28_q), .in28(register_29_q), .in29(register_30_q),
    .in30(register_31_q), .in31(register_32_q), .out(ReadData1), .sel(ReadRegister1));
  Multiplexer #(.select(5), .width(32), .disabled(0), .enable("false")) multiplexer_2 (
    .in0(register_1_q), .in1(register_2_q), .in2(register_3_q), .in3(register_4_q), .in4(register_5_q),
    .in5(register_6_q), .in6(register_7_q), .in7(register_8_q), .in8(register_9_q), .in9(register_10_q),
    .in10(register_11_q), .in11(register_12_q), .in12(register_13_q), .in13(register_14_q),
    .in14(register_15_q), .in15(register_16_q), .in16(register_17_q), .in17(register_18_q),
    .in18(register_19_q), .in19(register_20_q), .in20(register_21_q), .in21(register_22_q),
    .in22(register_23_q), .in23(register_24_q), .in24(register_25_q), .in25(register_26_q),
    .in26(register_27_q), .in27(register_28_q), .in28(register_29_q), .in29(register_30_q),
    .in30(register_31_q), .in31(register_32_q), .out(ReadData2), .sel(ReadRegister2));
endmodule

module SignExtend (
  input  [15:0] in_1,
  output [31:0] out_2
);


  assign out_2 = {{17{in_1[15]}}, in_1[14:0]};
endmodule

module ALUControl (
  input  [5:0] _31_26,
  input  [5:0] _5_0,
  output [2:0] out_3
);

  wire ADD_out, identifyop_1_add, identifyop_1_addi, identifyop_1_addiu, identifyop_1_and, identifyop_1_beq,
       identifyop_1_j, identifyop_1_lw, identifyop_1_or, identifyop_1_slt, identifyop_1_sub, identifyop_1_sw,
       SUB_out;

  IdentifyOp identifyop_1 (
    ._31_26(_31_26), ._5_0(_5_0), .ADD(identifyop_1_add), .SLT(identifyop_1_slt), .ADDIU(identifyop_1_addiu),
    .LW(identifyop_1_lw), .ADDI(identifyop_1_addi), .BEQ(identifyop_1_beq), .SW(identifyop_1_sw),
    .SUB(identifyop_1_sub), .AND(identifyop_1_and), .OR(identifyop_1_or), .J(identifyop_1_j));
  or ADD (ADD_out, identifyop_1_add, identifyop_1_addiu, identifyop_1_lw, identifyop_1_addi, identifyop_1_sw);
  or SUB (SUB_out, identifyop_1_beq, identifyop_1_sub);
  or _1 (out_3[1], ADD_out, SUB_out, identifyop_1_slt);
  or _2 (out_3[2], SUB_out, identifyop_1_slt);
  or _0 (out_3[0], identifyop_1_slt, identifyop_1_or);
endmodule

module ReducirBits (
  input  [31:0] in_1,
  output [4:0] out_2
);


  assign out_2 = in_1[4:0];
endmodule

module ReducirBits26 (
  input  [25:0] in_1,
  output [4:0] out_2
);


  assign out_2 = in_1[4:0];
endmodule
